// Logisim project DDCA expo.circ as structural Verilog: 1 circuit, main circuit main
module main (
  input  in_1,
  input  in_2,
  input  in_3,
  output out_4
);

  Multiplexer multiplexer_1 (.in0(in_1), .in1(in_2), .out(out_4), .sel(in_3));  // open: en

  // Notes on the sheet:
  //   Pin Verification (B)
  //   Constant 0
  //   Card Status (A)
  //   Io
  //   I1
endmodule
